// Logisim project ex6.circ as structural Verilog: 5 circuits, main circuit RotRight
module RotRight (
  input  [15:0] INPUT0,
  input  [3:0] AMOUNT,
  output [15:0] OUTPUT0
);

  wire [15:0] rot1_1_out_3, rot2_1_out_3, rot4_1_out_3;

  rot1 rot1_1 (.out_3(rot1_1_out_3), .in_1(INPUT0), .Ctl(AMOUNT[0]));
  rot2 rot2_1 (.out_3(rot2_1_out_3), .in_1(rot1_1_out_3), .Ctl(AMOUNT[1]));
  rot4 rot4_1 (.out_3(rot4_1_out_3), .in_1(rot2_1_out_3), .Ctl(AMOUNT[2]));
  rot8 rot8_1 (.out_3(OUTPUT0), .in_1(rot4_1_out_3), .Ctl(AMOUNT[3]));
endmodule

module rot1 (
  input  [15:0] in_1,
  input  Ctl,
  output [15:0] out_3
);

  wire not_1_out;

  not not_1 (not_1_out, Ctl);
  Multiplexer #(.enable("false"), .width(16)) multiplexer_1 (
    .in0({in_1[0], in_1[15:1]}), .in1(in_1), .out(out_3), .sel(not_1_out));
endmodule

module rot2 (
  input  [15:0] in_1,
  input  Ctl,
  output [15:0] out_3
);

  wire not_1_out;

  not not_1 (not_1_out, Ctl);
  Multiplexer #(.enable("false"), .width(16)) multiplexer_1 (
    .in0({in_1[1:0], in_1[15:2]}), .in1(in_1), .out(out_3), .sel(not_1_out));
endmodule

module rot4 (
  input  [15:0] in_1,
  input  Ctl,
  output [15:0] out_3
);

  wire not_1_out;

  not not_1 (not_1_out, Ctl);
  Multiplexer #(.enable("false"), .width(16)) multiplexer_1 (
    .in0({in_1[3:0], in_1[15:4]}), .in1(in_1), .out(out_3), .sel(not_1_out));
endmodule

module rot8 (
  input  [15:0] in_1,
  input  Ctl,
  output [15:0] out_3
);

  wire not_1_out;

  not not_1 (not_1_out, Ctl);
  Multiplexer #(.enable("false"), .width(16)) multiplexer_1 (
    .in0({in_1[7:0], in_1[15:8]}), .in1(in_1), .out(out_3), .sel(not_1_out));
endmodule
